# Fritzing sketch Circuit_Serial_display_r2 (saved by Fritzing 0.9.3b)

parts:
  LCD1 = LCD screen
  Part2 = Arduino Pro Mini (5V)
  J1 = Dagu DGServo 9g header connector (female) [package=THT]
  C1 = Electrolytic Capacitor [capacitance=10μF package="0605 [SMD, electrolytic]"]
  R1 = Resistor [tolerance=±5% resistance=680 package=THT]
  R2 = Resistor [tolerance=±5% resistance=220 package=THT]

nets:
  N1: LCD1.VSS, C1.-
  VDD: LCD1.VDD, Part2.VCC
  N2: LCD1.V0, C1.+, R1.Pin_1
  N3: LCD1.RS, Part2.D2
  N4: LCD1.E, Part2.D3
  GND: LCD1.DB1, Part2.GND, J1.gnd
  N5: LCD1.DB4, Part2.D4
  N6: LCD1.DB5, Part2.D5
  N7: LCD1.DB6, Part2.D6
  N8: LCD1.DB7, Part2.D7
  N9: LCD1.LED+, Part2.D8
  N10: LCD1.LED-, R2.Pin_1
  N11: Part2.RAW, J1.Vcc
  N12: Part2.D10, R1.Pin_0
  N13: Part2.D9, R2.Pin_0
  N14: Part2.RXI, J1.pulse

notes:
  1602 CHARACTER LCD
  LCD Contrast adjustmet: R1 and C1 can be replaced with 10k trimpot
  FROM CG SCALE
  R2 is for protection of the I/O pins 8/9 if the LCD back light LED current is more than 20mA.
  Or the LED can be connected to VCC/GND rather than pin 8/9
  PRO MINI
